# Fritzing sketch ld20 nrf5340dk circuit (saved by Fritzing 0.9.3b)
stripboards: 1
perfboards: 1

parts:
  Part1 = Arduino Uno (Rev3)
  R1 = Resistor [tolerance=±5% resistance=2.4k package=THT]
  R2 = Resistor [tolerance=±5% resistance=2.4k package=THT]

nets:
  N1: Part1.A4/SDA, R1.Pin_0
  N2: Part1.A5/SCL, R2.Pin_0
  N3: Part1.3V3, R2.Pin_1
